// Logisim project alu.circ as structural Verilog: 19 circuits, main circuit L_2x1_mux_e9a47848
module L_2x1_mux_e9a47848 (
  input  [31:0] in_1,
  input  [31:0] in_2,
  input  [31:0] in_3,
  output [31:0] out_4
);

  wire [31:0] and_1_out, and_2_out, not_1_out;

  assign not_1_out = ~in_2;  // NOT_Gate not_1, 32 bits wide
  assign and_1_out = in_1 & not_1_out;  // AND_Gate and_1, 32 bits wide
  assign and_2_out = in_2 & in_3;  // AND_Gate and_2, 32 bits wide
  assign out_4 = and_1_out | and_2_out;  // OR_Gate or_1, 32 bits wide
endmodule

module L_16x1_mux_36673231 (
  input  in_1,
  input  in_2,
  input  in_3,
  input  in_4,
  input  [31:0] in_5,
  input  [31:0] in_6,
  input  [31:0] in_7,
  input  [31:0] in_8,
  input  [31:0] in_9,
  input  [31:0] in_10,
  input  [31:0] in_11,
  input  [31:0] in_12,
  input  [31:0] in_13,
  input  [31:0] in_14,
  input  [31:0] in_15,
  input  [31:0] in_16,
  input  [31:0] in_17,
  input  [31:0] in_18,
  input  [31:0] in_19,
  input  [31:0] in_20,
  output [31:0] out_21
);

  wire [31:0] bit_repeater_1_out_2, bit_repeater_2_out_2, bit_repeater_3_out_2, bit_repeater_4_out_2,
       l_2x1_mux_e9a47848_1_out_4, l_2x1_mux_e9a47848_2_out_4, l_2x1_mux_e9a47848_3_out_4,
       l_2x1_mux_e9a47848_4_out_4, l_2x1_mux_e9a47848_5_out_4, l_2x1_mux_e9a47848_6_out_4,
       l_2x1_mux_e9a47848_7_out_4, l_2x1_mux_e9a47848_8_out_4, l_2x1_mux_e9a47848_9_out_4,
       l_2x1_mux_e9a47848_10_out_4, l_2x1_mux_e9a47848_11_out_4, l_2x1_mux_e9a47848_12_out_4,
       l_2x1_mux_e9a47848_13_out_4, l_2x1_mux_e9a47848_14_out_4;

  bit_repeater bit_repeater_1 (.in_1(in_1), .out_2(bit_repeater_1_out_2));
  L_2x1_mux_e9a47848 l_2x1_mux_e9a47848_1 (
    .in_2(bit_repeater_1_out_2), .in_1(in_5), .in_3(in_6), .out_4(l_2x1_mux_e9a47848_1_out_4));
  L_2x1_mux_e9a47848 l_2x1_mux_e9a47848_2 (
    .in_2(bit_repeater_1_out_2), .in_1(in_7), .in_3(in_8), .out_4(l_2x1_mux_e9a47848_2_out_4));
  L_2x1_mux_e9a47848 l_2x1_mux_e9a47848_3 (
    .in_2(bit_repeater_1_out_2), .in_1(in_9), .in_3(in_10), .out_4(l_2x1_mux_e9a47848_3_out_4));
  L_2x1_mux_e9a47848 l_2x1_mux_e9a47848_4 (
    .in_2(bit_repeater_1_out_2), .in_1(in_11), .in_3(in_12), .out_4(l_2x1_mux_e9a47848_4_out_4));
  L_2x1_mux_e9a47848 l_2x1_mux_e9a47848_5 (
    .in_2(bit_repeater_1_out_2), .in_1(in_13), .in_3(in_14), .out_4(l_2x1_mux_e9a47848_5_out_4));
  L_2x1_mux_e9a47848 l_2x1_mux_e9a47848_6 (
    .in_2(bit_repeater_1_out_2), .in_1(in_15), .in_3(in_16), .out_4(l_2x1_mux_e9a47848_6_out_4));
  L_2x1_mux_e9a47848 l_2x1_mux_e9a47848_7 (
    .in_2(bit_repeater_1_out_2), .in_1(in_17), .in_3(in_18), .out_4(l_2x1_mux_e9a47848_7_out_4));
  L_2x1_mux_e9a47848 l_2x1_mux_e9a47848_8 (
    .in_2(bit_repeater_1_out_2), .in_1(in_19), .in_3(in_20), .out_4(l_2x1_mux_e9a47848_8_out_4));
  bit_repeater bit_repeater_2 (.in_1(in_2), .out_2(bit_repeater_2_out_2));
  L_2x1_mux_e9a47848 l_2x1_mux_e9a47848_9 (
    .in_2(bit_repeater_2_out_2), .in_1(l_2x1_mux_e9a47848_1_out_4), .in_3(l_2x1_mux_e9a47848_2_out_4),
    .out_4(l_2x1_mux_e9a47848_9_out_4));
  L_2x1_mux_e9a47848 l_2x1_mux_e9a47848_10 (
    .in_2(bit_repeater_2_out_2), .in_1(l_2x1_mux_e9a47848_3_out_4), .in_3(l_2x1_mux_e9a47848_4_out_4),
    .out_4(l_2x1_mux_e9a47848_10_out_4));
  L_2x1_mux_e9a47848 l_2x1_mux_e9a47848_11 (
    .in_2(bit_repeater_2_out_2), .in_1(l_2x1_mux_e9a47848_5_out_4), .in_3(l_2x1_mux_e9a47848_6_out_4),
    .out_4(l_2x1_mux_e9a47848_11_out_4));
  L_2x1_mux_e9a47848 l_2x1_mux_e9a47848_12 (
    .in_2(bit_repeater_2_out_2), .in_1(l_2x1_mux_e9a47848_7_out_4), .in_3(l_2x1_mux_e9a47848_8_out_4),
    .out_4(l_2x1_mux_e9a47848_12_out_4));
  bit_repeater bit_repeater_3 (.in_1(in_3), .out_2(bit_repeater_3_out_2));
  L_2x1_mux_e9a47848 l_2x1_mux_e9a47848_13 (
    .in_2(bit_repeater_3_out_2), .in_1(l_2x1_mux_e9a47848_9_out_4), .in_3(l_2x1_mux_e9a47848_10_out_4),
    .out_4(l_2x1_mux_e9a47848_13_out_4));
  L_2x1_mux_e9a47848 l_2x1_mux_e9a47848_14 (
    .in_2(bit_repeater_3_out_2), .in_1(l_2x1_mux_e9a47848_11_out_4), .in_3(l_2x1_mux_e9a47848_12_out_4),
    .out_4(l_2x1_mux_e9a47848_14_out_4));
  bit_repeater bit_repeater_4 (.in_1(in_4), .out_2(bit_repeater_4_out_2));
  L_2x1_mux_e9a47848 l_2x1_mux_e9a47848_15 (
    .in_2(bit_repeater_4_out_2), .in_1(l_2x1_mux_e9a47848_13_out_4), .in_3(l_2x1_mux_e9a47848_14_out_4),
    .out_4(out_21));
endmodule

module add (
  input  [31:0] in_1,
  input  [31:0] in_2,
  output [31:0] out_3,
  output out_4
);

  Adder #(.width(32)) adder_1 (.a(in_1), .b(in_2), .out(out_3), .cout(out_4));  // open: cin
endmodule

module sub (
  input  [31:0] in_1,
  input  [31:0] in_2,
  output [31:0] out_3
);

  Subtractor #(.width(32)) subtractor_1 (.a(in_1), .b(in_2), .out(out_3));  // open: bin, bout
endmodule

module sll (
  input  [31:0] in_1,
  input  [31:0] in_2,
  output [31:0] out_3
);

  wire [4:0] bit_extender_1_out;

  Bit_Extender #(.in_width(32), .out_width(5)) bit_extender_1 (.in(in_2), .out(bit_extender_1_out));
  Shifter #(.width(32)) shifter_1 (.in(in_1), .\dist (bit_extender_1_out), .out(out_3));
endmodule

module slt (
  input  [31:0] in_1,
  input  [31:0] in_2,
  output [31:0] out_3
);

  wire comparator_1_lt;

  Comparator #(.width(32)) comparator_1 (.a(in_1), .b(in_2), .lt(comparator_1_lt));  // open: gt, eq
  assign out_3 = {{31{comparator_1_lt}}, comparator_1_lt};  // Bit_Extender bit_extender_1
endmodule

module \xor  (
  input  [31:0] in_1,
  input  [31:0] in_2,
  output [31:0] out_3
);

  assign out_3 = in_1 ^ in_2;  // XOR_Gate xor_1, 32 bits wide
endmodule

module \and  (
  input  [31:0] in_1,
  input  [31:0] in_2,
  output [31:0] out_3
);

  assign out_3 = in_1 & in_2;  // AND_Gate and_1, 32 bits wide
endmodule

module alu1 (
  input  [31:0] in_1,
  input  [31:0] in_2,
  input  [3:0] in_3,
  output out_4,
  output [31:0] OUTPUT,
  output OVERFLOW
);

  wire add_1_out_4, not_1_out, not_2_out, not_3_out, not_4_out;
  wire [31:0] add_1_out_3, and_1_out_3, or_1_out_3, sll_1_out_3, slt_1_out_3, sltu_1_out_3, srl_1_out_3,
       sub_1_out_3, xor_1_out_3;

  add add_1 (.in_2(in_2), .in_1(in_1), .out_4(add_1_out_4), .out_3(add_1_out_3));
  sll sll_1 (.in_1(in_1), .in_2(in_2), .out_3(sll_1_out_3));
  slt slt_1 (.in_1(in_1), .in_2(in_2), .out_3(slt_1_out_3));
  sltu sltu_1 (.in_1(in_1), .in_2(in_2), .out_3(sltu_1_out_3));
  \xor  xor_1 (.in_1(in_1), .in_2(in_2), .out_3(xor_1_out_3));
  srl srl_1 (.in_1(in_1), .in_2(in_2), .out_3(srl_1_out_3));
  \or  or_1 (.in_1(in_1), .in_2(in_2), .out_3(or_1_out_3));
  \and  and_1 (.in_1(in_1), .in_2(in_2), .out_3(and_1_out_3));
  sub sub_1 (.in_1(in_1), .in_2(in_2), .out_3(sub_1_out_3));
  L_16x1_mux_36673231 l_16x1_mux_36673231_1 (
    .in_1(in_3[0]), .in_2(in_3[1]), .in_3(in_3[2]), .in_4(in_3[3]), .in_13(sub_1_out_3), .in_5(add_1_out_3),
    .in_6(sll_1_out_3), .in_7(slt_1_out_3), .in_8(sltu_1_out_3), .in_9(xor_1_out_3), .in_10(srl_1_out_3),
    .in_11(or_1_out_3), .in_12(and_1_out_3), .out_21(OUTPUT));  // open: in_14, in_15, in_16, in_17, in_18, in_19, in_20
  not not_1 (not_1_out, in_3[2]);
  not not_2 (not_2_out, in_3[3]);
  zero zero_1 (.in_1(OUTPUT), .out_2(out_4));
  not not_3 (not_3_out, in_3[0]);
  not not_4 (not_4_out, in_3[1]);
  and and_2 (OVERFLOW, add_1_out_4, not_2_out);

  // Notes on the sheet:
  //   A
  //   B
endmodule

module bit_repeater (
  input  in_1,
  output [31:0] out_2
);

  wire [31:0] bit_extender_1_out, shifter_1_out;

  assign bit_extender_1_out = {{31{in_1}}, in_1};  // Bit_Extender bit_extender_1
  Shifter #(.width(32)) shifter_1 (.in(bit_extender_1_out), .\dist ({5{1'b1}}), .out(shifter_1_out));
  Shifter #(.shift("ar"), .width(32)) shifter_2 (.in(shifter_1_out), .\dist ({5{1'b1}}), .out(out_2));
endmodule

module \or  (
  input  [31:0] in_1,
  input  [31:0] in_2,
  output [31:0] out_3
);

  assign out_3 = in_1 | in_2;  // OR_Gate or_1, 32 bits wide
endmodule

module sra (
  input  [31:0] in_1,
  input  [31:0] in_2,
  output [31:0] out_3
);

  wire [4:0] bit_extender_1_out;

  Bit_Extender #(.in_width(32), .out_width(5)) bit_extender_1 (.in(in_2), .out(bit_extender_1_out));
  Shifter #(.shift("ar"), .width(32)) shifter_1 (.in(in_1), .\dist (bit_extender_1_out), .out(out_3));
endmodule

module mul (
  input  [31:0] in_1,
  input  [31:0] in_2,
  output [31:0] out_3
);

  Multiplier #(.width(32)) multiplier_1 (.a(in_1), .b(in_2), .out(out_3));  // open: cin, cout
endmodule

module mulh (
  input  [31:0] in_1,
  input  [31:0] in_2,
  output [31:0] out_3
);

  Multiplier #(.width(32)) multiplier_1 (.a(in_1), .b(in_2), .cout(out_3));  // open: out, cin
endmodule

module mulhu (
  input  [31:0] in_1,
  input  [31:0] in_2,
  output [31:0] out_3
);

  wire [31:0] adder_1_out, adder_2_out, adder_3_out, adder_4_out, and_1_out, and_2_out, and_3_out, and_4_out,
       and_5_out, and_6_out, and_7_out, and_8_out, and_9_out, multiplier_1_out, multiplier_2_out,
       multiplier_3_out, multiplier_4_out, shifter_1_out, shifter_2_out, shifter_3_out, shifter_4_out,
       shifter_5_out, shifter_6_out;

  assign and_1_out = 32'hffff0000 & in_1;  // AND_Gate and_1, 32 bits wide
  assign and_2_out = in_1 & 32'hffff;  // AND_Gate and_2, 32 bits wide
  assign and_3_out = 32'hffff0000 & in_2;  // AND_Gate and_3, 32 bits wide
  assign and_4_out = in_2 & 32'hffff;  // AND_Gate and_4, 32 bits wide
  Shifter #(.shift("lr"), .width(32)) shifter_1 (.in(and_1_out), .\dist (5'b10000), .out(shifter_1_out));
  Shifter #(.shift("lr"), .width(32)) shifter_2 (.in(and_3_out), .\dist (5'b10000), .out(shifter_2_out));
  Multiplier #(.width(32)) multiplier_1 (
    .a(shifter_1_out), .b(shifter_2_out), .out(multiplier_1_out));  // open: cin, cout
  Multiplier #(.width(32)) multiplier_2 (.a(shifter_2_out), .b(and_2_out), .out(multiplier_2_out));  // open: cin, cout
  Multiplier #(.width(32)) multiplier_3 (.a(shifter_1_out), .b(and_4_out), .out(multiplier_3_out));  // open: cin, cout
  Multiplier #(.width(32)) multiplier_4 (.a(and_2_out), .b(and_4_out), .out(multiplier_4_out));  // open: cin, cout
  assign and_5_out = multiplier_4_out & 32'hffff0000;  // AND_Gate and_5, 32 bits wide
  assign and_6_out = multiplier_2_out & 32'hffff;  // AND_Gate and_6, 32 bits wide
  assign and_7_out = multiplier_3_out & 32'hffff;  // AND_Gate and_7, 32 bits wide
  Shifter #(.shift("lr"), .width(32)) shifter_3 (.in(and_5_out), .\dist (5'b10000), .out(shifter_3_out));
  assign and_8_out = 32'hffff0000 & multiplier_2_out;  // AND_Gate and_8, 32 bits wide
  assign and_9_out = 32'hffff0000 & multiplier_3_out;  // AND_Gate and_9, 32 bits wide
  Adder #(.width(32)) adder_1 (.a(and_6_out), .b(adder_2_out), .out(adder_1_out));  // open: cin, cout
  Adder #(.width(32)) adder_2 (.a(and_7_out), .b(shifter_3_out), .out(adder_2_out));  // open: cin, cout
  Shifter #(.shift("lr"), .width(32)) shifter_4 (.in(and_8_out), .\dist (5'b10000), .out(shifter_4_out));
  Shifter #(.shift("lr"), .width(32)) shifter_5 (.in(and_9_out), .\dist (5'b10000), .out(shifter_5_out));
  Shifter #(.shift("lr"), .width(32)) shifter_6 (.in(adder_1_out), .\dist (5'b10000), .out(shifter_6_out));
  Adder #(.width(32)) adder_3 (.a(shifter_4_out), .b(shifter_5_out), .out(adder_3_out));  // open: cin, cout
  Adder #(.width(32)) adder_4 (.a(shifter_6_out), .b(adder_3_out), .out(adder_4_out));  // open: cin, cout
  Adder #(.width(32)) adder_5 (.a(multiplier_1_out), .b(adder_4_out), .out(out_3));  // open: cin, cout

  // Notes on the sheet:
  //   A
  //   B
  //   la
  //   lb
  //   ha
  //   hb
  //   ha*hb
  //   la*hb
  //   ha*lb
  //   la*lb
  //   h(la*lb)
endmodule

module bsel (
  input  [31:0] in_1,
  input  [31:0] in_2,
  output [31:0] out_3
);

  wire [31:0] and_1_out, and_2_out, not_1_out;

  assign not_1_out = ~{32{1'b1}};  // NOT_Gate not_1, 32 bits wide
  assign and_1_out = in_1 & not_1_out;  // AND_Gate and_1, 32 bits wide
  assign and_2_out = {32{1'b1}} & in_2;  // AND_Gate and_2, 32 bits wide
  assign out_3 = and_1_out | and_2_out;  // OR_Gate or_1, 32 bits wide
endmodule

module srl (
  input  [31:0] in_1,
  input  [31:0] in_2,
  output [31:0] out_3
);

  wire [4:0] bit_extender_1_out;

  Bit_Extender #(.in_width(32), .out_width(5)) bit_extender_1 (.in(in_2), .out(bit_extender_1_out));
  Shifter #(.shift("lr"), .width(32)) shifter_1 (.in(in_1), .\dist (bit_extender_1_out), .out(out_3));
endmodule

module zero (
  input  [31:0] in_1,
  output out_2
);

  Comparator #(.width(32)) comparator_1 (.a(in_1), .b({32{1'b0}}), .eq(out_2));  // open: gt, lt
endmodule

module sltu (
  input  [31:0] in_1,
  input  [31:0] in_2,
  output [31:0] out_3
);

  wire and_1_out, comparator_1_eq, comparator_1_lt, comparator_2_lt, or_1_out;

  Comparator #(.width(16)) comparator_1 (
    .a(in_1[31:16]), .b(in_2[31:16]), .eq(comparator_1_eq), .lt(comparator_1_lt));  // open: gt
  Comparator #(.width(16)) comparator_2 (.a(in_1[15:0]), .b(in_2[15:0]), .lt(comparator_2_lt));  // open: gt, eq
  and and_1 (and_1_out, comparator_1_eq, comparator_2_lt);
  assign out_3 = {{31{1'b0}}, or_1_out};  // Bit_Extender bit_extender_1
  or or_1 (or_1_out, and_1_out, comparator_1_lt);
endmodule
