// Logisim project proc4.circ as structural Verilog: 7 circuits, main circuit control
module control (
  input  [6:0] in_1,
  output [1:0] ALUOp0,
  output out_3,
  output Branch___a,
  output out_5,
  output out_6,
  output out_7
);

  wire and_1_out, and_2_out, and_3_out, and_4_out, and_5_out, and_6_out, not_1_out, not_2_out, not_3_out,
       not_4_out, not_5_out, not_6_out, or_1_out, or_2_out;

  not not_1 (not_1_out, in_1[2]);
  not not_2 (not_2_out, in_1[3]);
  not not_3 (not_3_out, in_1[4]);
  not not_4 (not_4_out, in_1[6]);
  and and_1 (and_1_out, in_1[0], in_1[1], not_1_out, not_2_out);
  not not_5 (not_5_out, in_1[5]);
  not not_6 (not_6_out, in_1[4]);
  and and_2 (and_2_out, in_1[4], in_1[5]);
  and and_3 (and_3_out, in_1[5], not_4_out, not_3_out);
  and and_4 (and_4_out, not_4_out, not_3_out);
  and and_5 (and_5_out, not_4_out, not_5_out, in_1[4]);
  and and_6 (and_6_out, not_5_out, not_6_out);
  or or_1 (or_1_out, not_5_out, and_2_out);
  or or_2 (or_2_out, and_4_out, and_5_out);
  and and_7 (ALUOp0[0], in_1[6], and_1_out);
  and and_8 (ALUOp0[1], in_1[4], and_1_out);
  and and_9 (out_3, and_6_out, and_1_out);
  and and_10 (Branch___a, in_1[6], and_1_out);
  and and_11 (out_5, or_1_out, and_1_out);
  and and_12 (out_6, and_3_out, and_1_out);
  and and_13 (out_7, and_1_out, or_2_out);

  // Notes on the sheet:
  //   g
  //   f
  //   e
  //   d
  //   c
  //   b
  //   a
  //   d'e'fg
  //   MemtoReg - b'c'
  //   MemWrite - a'bc'
  //   ALUSrc - ac'+a'b'c
  //   RegWrite - b xnor c
endmodule

module imem (
  input  [7:0] in_1,
  input  in_2,
  output [31:0] out_3
);

  RAM #(.dataWidth(32)) ram_1 (.addr(in_1), .oe(1'b1), .clk(in_2), .dout(out_3));  // open: we, din
endmodule

module DataMem (
  input  [7:0] in_1,
  input  in_2,
  input  in_3,
  input  [31:0] in_4,
  output [31:0] out_5
);

  RAM #(.asyncread("true"), .dataWidth(32)) ram_1 (
    .addr(in_1), .we(in_2), .oe(1'b1), .clk(in_3), .din(in_4), .dout(out_5));
endmodule

module ImmGen (
  input  [31:0] in_1,
  output [31:0] out_2
);

  wire [1:0] bit_extender_1_out;
  wire [31:0] and_1_out, and_2_out, and_3_out, and_4_out, and_5_out, and_6_out, and_7_out, and_8_out,
       or_1_out, or_2_out, shifter_1_out, shifter_2_out, shifter_3_out, shifter_4_out, shifter_5_out,
       shifter_6_out, shifter_7_out;

  assign and_1_out = 32'h80000000 & in_1;  // AND_Gate and_1, 32 bits wide
  assign and_2_out = in_1 & 32'h60;  // AND_Gate and_2, 32 bits wide
  assign and_3_out = 32'hf80 & in_1;  // AND_Gate and_3, 32 bits wide
  assign and_4_out = 32'hfe000000 & in_1;  // AND_Gate and_4, 32 bits wide
  Shifter #(.shift("lr"), .width(32)) shifter_1 (.in(in_1), .\dist (5'b10100), .out(shifter_1_out));
  Shifter #(.shift("lr"), .width(32)) shifter_2 (.in(and_2_out), .\dist (5'b00101), .out(shifter_2_out));
  Shifter #(.shift("rr"), .width(32)) shifter_3 (.in(and_1_out), .\dist (5'b10011), .out(shifter_3_out));
  assign and_5_out = 32'h1 & shifter_6_out;  // AND_Gate and_5, 32 bits wide
  Shifter #(.shift("lr"), .width(32)) shifter_4 (.in(and_4_out), .\dist (5'b10100), .out(shifter_4_out));
  Bit_Extender #(.in_width(32), .out_width(2)) bit_extender_1 (.in(shifter_2_out), .out(bit_extender_1_out));
  Shifter #(.width(32)) shifter_5 (.in(and_5_out), .\dist (5'b01011), .out(shifter_5_out));
  Shifter #(.shift("lr"), .width(32)) shifter_6 (.in(and_3_out), .\dist (5'b00111), .out(shifter_6_out));
  assign and_6_out = shifter_4_out & 32'hffffffe0;  // AND_Gate and_6, 32 bits wide
  assign and_7_out = shifter_6_out & 32'hfffffffe;  // AND_Gate and_7, 32 bits wide
  assign or_1_out = shifter_6_out | and_6_out;  // OR_Gate or_1, 32 bits wide
  assign and_8_out = and_6_out & 32'hfffff7ff;  // AND_Gate and_8, 32 bits wide
  Shifter #(.shift("lr"), .width(32)) shifter_7 (.in(or_2_out), .\dist (5'b00001), .out(shifter_7_out));
  assign or_2_out = shifter_3_out | shifter_5_out | and_7_out | and_8_out;  // OR_Gate or_2, 32 bits wide
  Multiplexer #(.select(2), .width(32)) multiplexer_1 (
    .in0(shifter_1_out), .in1(or_1_out), .in3(shifter_7_out), .out(out_2), .sel(bit_extender_1_out));  // open: in2
  Demultiplexer demultiplexer_1 ();  // open: out0, out1, in, sel

  // Notes on the sheet:
  //   b12
  //   b11
endmodule

module register_file (
  input  in_1,
  input  [31:0] in_2,
  input  in_3,
  input  [4:0] in_4,
  input  [4:0] in_5,
  input  [4:0] in_6,
  output [31:0] out_7,
  output [31:0] out_8
);

  wire and_1_out, and_2_out, and_3_out, and_4_out, and_5_out, and_6_out, and_7_out, and_8_out, and_9_out,
       and_10_out, and_11_out, and_12_out, and_13_out, and_14_out, and_15_out, and_16_out, and_17_out,
       and_18_out, and_19_out, and_20_out, and_21_out, and_22_out, and_23_out, and_24_out, and_25_out,
       and_26_out, and_27_out, and_28_out, and_29_out, and_30_out, and_31_out, and_32_out, decoder_1_out0,
       decoder_1_out1, decoder_1_out2, decoder_1_out3, decoder_1_out4, decoder_1_out5, decoder_1_out6,
       decoder_1_out7, decoder_1_out8, decoder_1_out9, decoder_1_out10, decoder_1_out11, decoder_1_out12,
       decoder_1_out13, decoder_1_out14, decoder_1_out15, decoder_1_out16, decoder_1_out17, decoder_1_out18,
       decoder_1_out19, decoder_1_out20, decoder_1_out21, decoder_1_out22, decoder_1_out23, decoder_1_out24,
       decoder_1_out25, decoder_1_out26, decoder_1_out27, decoder_1_out28, decoder_1_out29, decoder_1_out30,
       decoder_1_out31;
  wire [31:0] register_1_q, register_2_q, register_3_q, register_4_q, register_5_q, register_6_q,
       register_7_q, register_8_q, register_9_q, register_10_q, register_11_q, register_12_q, register_13_q,
       register_14_q, register_15_q, register_16_q, register_17_q, register_18_q, register_19_q,
       register_20_q, register_21_q, register_22_q, register_23_q, register_24_q, register_25_q,
       register_26_q, register_27_q, register_28_q, register_29_q, register_30_q, register_31_q,
       register_32_q;

  Decoder #(.select(5)) decoder_1 (
    .out0(decoder_1_out0), .out1(decoder_1_out1), .out2(decoder_1_out2), .out3(decoder_1_out3),
    .out4(decoder_1_out4), .out5(decoder_1_out5), .out6(decoder_1_out6), .out7(decoder_1_out7),
    .out8(decoder_1_out8), .out9(decoder_1_out9), .out10(decoder_1_out10), .out11(decoder_1_out11),
    .out12(decoder_1_out12), .out13(decoder_1_out13), .out14(decoder_1_out14), .out15(decoder_1_out15),
    .out16(decoder_1_out16), .out17(decoder_1_out17), .out18(decoder_1_out18), .out19(decoder_1_out19),
    .out20(decoder_1_out20), .out21(decoder_1_out21), .out22(decoder_1_out22), .out23(decoder_1_out23),
    .out24(decoder_1_out24), .out25(decoder_1_out25), .out26(decoder_1_out26), .out27(decoder_1_out27),
    .out28(decoder_1_out28), .out29(decoder_1_out29), .out30(decoder_1_out30), .out31(decoder_1_out31),
    .sel(in_6));  // open: en
  and and_1 (and_1_out, decoder_1_out0, in_1);
  and and_2 (and_2_out, decoder_1_out4, in_1);
  and and_3 (and_3_out, decoder_1_out8, in_1);
  and and_4 (and_4_out, decoder_1_out12, in_1);
  and and_5 (and_5_out, decoder_1_out16, in_1);
  and and_6 (and_6_out, decoder_1_out20, in_1);
  and and_7 (and_7_out, decoder_1_out24, in_1);
  and and_8 (and_8_out, decoder_1_out28, in_1);
  Register #(.width(32)) register_1 (.D(in_2), .en(and_1_out), .clk(in_3), .Q(register_1_q), .clr(1'b1));
  Register #(.width(32)) register_2 (.D(in_2), .en(and_2_out), .clk(in_3), .Q(register_2_q));  // open: clr
  Register #(.width(32)) register_3 (.D(in_2), .en(and_3_out), .clk(in_3), .Q(register_3_q));  // open: clr
  Register #(.width(32)) register_4 (.D(in_2), .en(and_4_out), .clk(in_3), .Q(register_4_q));  // open: clr
  Register #(.width(32)) register_5 (.D(in_2), .en(and_5_out), .clk(in_3), .Q(register_5_q));  // open: clr
  Register #(.width(32)) register_6 (.D(in_2), .en(and_6_out), .clk(in_3), .Q(register_6_q));  // open: clr
  Register #(.width(32)) register_7 (.D(in_2), .en(and_7_out), .clk(in_3), .Q(register_7_q));  // open: clr
  Register #(.width(32)) register_8 (.D(in_2), .en(and_8_out), .clk(in_3), .Q(register_8_q));  // open: clr
  Register #(.width(32)) register_9 (.D(in_2), .en(and_9_out), .clk(in_3), .Q(register_9_q));  // open: clr
  and and_9 (and_9_out, decoder_1_out1, in_1);
  Register #(.width(32)) register_10 (.D(in_2), .en(and_10_out), .clk(in_3), .Q(register_10_q));  // open: clr
  and and_10 (and_10_out, decoder_1_out5, in_1);
  Register #(.width(32)) register_11 (.D(in_2), .en(and_11_out), .clk(in_3), .Q(register_11_q));  // open: clr
  and and_11 (and_11_out, decoder_1_out9, in_1);
  and and_12 (and_12_out, decoder_1_out13, in_1);
  Register #(.width(32)) register_12 (.D(in_2), .en(and_13_out), .clk(in_3), .Q(register_12_q));  // open: clr
  and and_13 (and_13_out, decoder_1_out17, in_1);
  Register #(.width(32)) register_13 (.D(in_2), .en(and_14_out), .clk(in_3), .Q(register_13_q));  // open: clr
  and and_14 (and_14_out, decoder_1_out21, in_1);
  Register #(.width(32)) register_14 (.D(in_2), .en(and_15_out), .clk(in_3), .Q(register_14_q));  // open: clr
  and and_15 (and_15_out, decoder_1_out25, in_1);
  Register #(.width(32)) register_15 (.D(in_2), .en(and_16_out), .clk(in_3), .Q(register_15_q));  // open: clr
  and and_16 (and_16_out, decoder_1_out29, in_1);
  Register #(.width(32)) register_16 (.D(in_2), .en(and_12_out), .clk(in_3), .Q(register_16_q));  // open: clr
  and and_17 (and_17_out, decoder_1_out2, in_1);
  and and_18 (and_18_out, decoder_1_out6, in_1);
  and and_19 (and_19_out, decoder_1_out10, in_1);
  and and_20 (and_20_out, decoder_1_out14, in_1);
  and and_21 (and_21_out, decoder_1_out18, in_1);
  and and_22 (and_22_out, decoder_1_out22, in_1);
  and and_23 (and_23_out, decoder_1_out26, in_1);
  and and_24 (and_24_out, decoder_1_out30, in_1);
  Register #(.width(32)) register_17 (.D(in_2), .en(and_17_out), .clk(in_3), .Q(register_17_q));  // open: clr
  Register #(.width(32)) register_18 (.D(in_2), .en(and_18_out), .clk(in_3), .Q(register_18_q));  // open: clr
  Register #(.width(32)) register_19 (.D(in_2), .en(and_19_out), .clk(in_3), .Q(register_19_q));  // open: clr
  Register #(.width(32)) register_20 (.D(in_2), .en(and_20_out), .clk(in_3), .Q(register_20_q));  // open: clr
  Register #(.width(32)) register_21 (.D(in_2), .en(and_21_out), .clk(in_3), .Q(register_21_q));  // open: clr
  Register #(.width(32)) register_22 (.D(in_2), .en(and_22_out), .clk(in_3), .Q(register_22_q));  // open: clr
  Register #(.width(32)) register_23 (.D(in_2), .en(and_23_out), .clk(in_3), .Q(register_23_q));  // open: clr
  Register #(.width(32)) register_24 (.D(in_2), .en(and_24_out), .clk(in_3), .Q(register_24_q));  // open: clr
  and and_25 (and_25_out, decoder_1_out3, in_1);
  and and_26 (and_26_out, decoder_1_out7, in_1);
  and and_27 (and_27_out, decoder_1_out11, in_1);
  and and_28 (and_28_out, decoder_1_out15, in_1);
  and and_29 (and_29_out, decoder_1_out19, in_1);
  and and_30 (and_30_out, decoder_1_out23, in_1);
  and and_31 (and_31_out, decoder_1_out27, in_1);
  and and_32 (and_32_out, decoder_1_out31, in_1);
  Register #(.width(32)) register_25 (.D(in_2), .en(and_25_out), .clk(in_3), .Q(register_25_q));  // open: clr
  Register #(.width(32)) register_26 (.D(in_2), .en(and_26_out), .clk(in_3), .Q(register_26_q));  // open: clr
  Register #(.width(32)) register_27 (.D(in_2), .en(and_27_out), .clk(in_3), .Q(register_27_q));  // open: clr
  Register #(.width(32)) register_28 (.D(in_2), .en(and_28_out), .clk(in_3), .Q(register_28_q));  // open: clr
  Register #(.width(32)) register_29 (.D(in_2), .en(and_29_out), .clk(in_3), .Q(register_29_q));  // open: clr
  Register #(.width(32)) register_30 (.D(in_2), .en(and_30_out), .clk(in_3), .Q(register_30_q));  // open: clr
  Register #(.width(32)) register_31 (.D(in_2), .en(and_31_out), .clk(in_3), .Q(register_31_q));  // open: clr
  Register #(.width(32)) register_32 (.D(in_2), .en(and_32_out), .clk(in_3), .Q(register_32_q));  // open: clr
  Multiplexer #(.select(5), .width(32)) multiplexer_1 (
    .in0(register_1_q), .in1(register_9_q), .in2(register_17_q), .in3(register_25_q), .in4(register_2_q),
    .in5(register_10_q), .in6(register_18_q), .in7(register_26_q), .in8(register_3_q), .in9(register_11_q),
    .in10(register_19_q), .in11(register_27_q), .in12(register_4_q), .in13(register_16_q),
    .in14(register_20_q), .in15(register_28_q), .in16(register_5_q), .in17(register_12_q),
    .in18(register_21_q), .in19(register_29_q), .in20(register_6_q), .in21(register_13_q),
    .in22(register_22_q), .in23(register_30_q), .in24(register_7_q), .in25(register_14_q),
    .in26(register_23_q), .in27(register_31_q), .in28(register_8_q), .in29(register_15_q),
    .in30(register_24_q), .in31(register_32_q), .out(out_7), .sel(in_4));
  Multiplexer #(.select(5), .width(32)) multiplexer_2 (
    .in0(register_1_q), .in1(register_9_q), .in2(register_17_q), .in3(register_25_q), .in4(register_2_q),
    .in5(register_10_q), .in6(register_18_q), .in7(register_26_q), .in8(register_3_q), .in9(register_11_q),
    .in10(register_19_q), .in11(register_27_q), .in12(register_4_q), .in13(register_16_q),
    .in14(register_20_q), .in15(register_28_q), .in16(register_5_q), .in17(register_12_q),
    .in18(register_21_q), .in19(register_29_q), .in20(register_6_q), .in21(register_13_q),
    .in22(register_22_q), .in23(register_30_q), .in24(register_7_q), .in25(register_14_q),
    .in26(register_23_q), .in27(register_31_q), .in28(register_8_q), .in29(register_15_q),
    .in30(register_24_q), .in31(register_32_q), .out(out_8), .sel(in_5));
endmodule

module alu_control (
  input  [3:0] in_1,
  input  [1:0] in_2,
  output [3:0] out_3
);

  Multiplexer #(.select(2), .width(4)) multiplexer_1 (
    .in0(4'b0000), .in1(4'b1000), .in2(in_1), .out(out_3), .sel(in_2));  // open: in3
endmodule

module main2 (
  input  in_1
);

  wire alu1_1_out_4, and_1_out, clock_1_out, control_1_branch___a, control_1_out_3, control_1_out_5,
       control_1_out_6, control_1_out_7;
  wire [1:0] control_1_aluop0;
  wire [3:0] alu_control_1_out_3;
  wire [7:0] adder_1_out, adder_2_out, bit_extender_1_out, bit_extender_2_out, multiplexer_2_out,
       register_1_q;
  wire [31:0] alu1_1_output, datamem_1_out_5, imem_1_out_3, immgen_1_out_2, multiplexer_1_out,
       multiplexer_3_out, register_file_1_out_7, register_file_1_out_8;

  Register register_1 (.D(multiplexer_2_out), .en(in_1), .clk(clock_1_out), .Q(register_1_q));  // open: clr
  // Probe on register_1_q
  // Probe on imem_1_out_3
  // Probe on imem_1_out_3[19:15]
  // Probe on imem_1_out_3[24:20]
  // Probe on imem_1_out_3[11:7]
  // Probe on register_file_1_out_7
  // Probe on register_file_1_out_8
  // Probe on immgen_1_out_2
  // Probe on alu_control_1_out_3
  // Probe on alu1_1_output
  // Probe on datamem_1_out_5
  // Probe on multiplexer_3_out
  imem imem_1 (.in_2(clock_1_out), .in_1(register_1_q), .out_3(imem_1_out_3));
  Adder adder_1 (.a(register_1_q), .b(8'h1), .out(adder_1_out));  // open: cin, cout
  control control_1 (
    .in_1(imem_1_out_3[6:0]), .out_3(control_1_out_3), .Branch___a(control_1_branch___a),
    .out_5(control_1_out_5), .out_6(control_1_out_6), .out_7(control_1_out_7), .ALUOp0(control_1_aluop0));
  register_file register_file_1 (
    .in_6(imem_1_out_3[11:7]), .in_1(control_1_out_5), .in_2(multiplexer_3_out), .in_3(clock_1_out),
    .in_4(imem_1_out_3[19:15]), .in_5(imem_1_out_3[24:20]), .out_7(register_file_1_out_7),
    .out_8(register_file_1_out_8));
  ImmGen immgen_1 (.in_1(imem_1_out_3), .out_2(immgen_1_out_2));
  Bit_Extender #(.in_width(32), .out_width(8), .\type ("zero")) bit_extender_1 (
    .in(immgen_1_out_2), .out(bit_extender_1_out));
  Multiplexer #(.width(32)) multiplexer_1 (
    .in0(register_file_1_out_8), .in1(immgen_1_out_2), .out(multiplexer_1_out), .sel(control_1_out_7));
  alu_control alu_control_1 (
    .in_1({imem_1_out_3[30], imem_1_out_3[14:12]}), .in_2(control_1_aluop0), .out_3(alu_control_1_out_3));
  alu1 alu1_1 (
    .in_2(multiplexer_1_out), .in_1(register_file_1_out_7), .in_3(alu_control_1_out_3), .out_4(alu1_1_out_4),
    .OUTPUT(alu1_1_output));  // open: OVERFLOW
  Clock clock_1 (.out(clock_1_out));
  Bit_Extender #(.in_width(32), .out_width(8), .\type ("zero")) bit_extender_2 (
    .in(alu1_1_output), .out(bit_extender_2_out));
  Adder adder_2 (.a(register_1_q), .b(bit_extender_1_out), .out(adder_2_out));  // open: cin, cout
  and and_1 (and_1_out, alu1_1_out_4, control_1_branch___a);
  Multiplexer #(.width(8)) multiplexer_2 (
    .in0(adder_1_out), .in1(adder_2_out), .out(multiplexer_2_out), .sel(and_1_out));
  DataMem datamem_1 (
    .in_3(clock_1_out), .in_4(register_file_1_out_8), .in_2(control_1_out_6), .in_1(bit_extender_2_out),
    .out_5(datamem_1_out_5));
  Multiplexer #(.width(32)) multiplexer_3 (
    .in0(alu1_1_output), .in1(datamem_1_out_5), .out(multiplexer_3_out), .sel(control_1_out_3));

  // Notes on the sheet:
  //   IAddr
  //   Instruction
  //   rs1
  //   rd
  //   Data1
  //   Data2
  //   Imm
  //   ALUCtrl
  //   ALUOut
  //   DataOut
  //   WriteData
  //   rs2
  //   MemtoReg
  //   ALUOp
  //   MemWrite
  //   ALUSrc
  //   RegWrite
endmodule
